# Fritzing sketch CodeGamePCB (saved by Fritzing 0.9.2b)
circuit board: 5.68443cm x 3.33492cm
breadboards: 1

parts:
  -_+_P_B_A = female pin header, 5 pins [form="♀ (female)"]
  -_+_P_B_A_2 = female pin header, 5 pins [form="♀ (female)"]
  +_- = Piezo Speaker
  Arduino = Arduino Pro Mini v13
  O_L_S_I_D_R_C_-_+ = female pin header, 9 pins [form="♀ (female)"]
  +_-_2 = female pin header, 2 pins [form="♀ (female)"]
  I/O = female pin header, 3 pins [form="♀ (female)"]

nets:
  N1: -_+_P_B_A.pin1, Arduino.D2
  N2: -_+_P_B_A.pin2, Arduino.D4
  N3: -_+_P_B_A.pin3, Arduino.A1
  N4: -_+_P_B_A.pin4, -_+_P_B_A_2.pin4, Arduino.VCC, O_L_S_I_D_R_C_-_+.pin2, O_L_S_I_D_R_C_-_+.pin9
  N5: -_+_P_B_A.pin5, -_+_P_B_A_2.pin5, +_-.pin2, Arduino.GND, O_L_S_I_D_R_C_-_+.pin8, +_-_2.pin2
  N6: -_+_P_B_A_2.pin1, Arduino.D3_PWM
  N7: -_+_P_B_A_2.pin2, Arduino.D5_PWM
  N8: -_+_P_B_A_2.pin3, Arduino.A0
  N9: +_-.pin1, Arduino.D6_PWM
  N10: Arduino.RAW, I/O.pin1, I/O.pin2
  N11: Arduino.D13/SCK, O_L_S_I_D_R_C_-_+.pin3
  N12: Arduino.D11_PWM/MOSI, O_L_S_I_D_R_C_-_+.pin4
  N13: Arduino.D10_PWM/SS, O_L_S_I_D_R_C_-_+.pin7
  N14: Arduino.D9_PWM, O_L_S_I_D_R_C_-_+.pin5
  N15: Arduino.D8, O_L_S_I_D_R_C_-_+.pin6
  N16: +_-_2.pin1, I/O.pin3

notes:
  CodeGame
